# Fritzing sketch Receiver (saved by Fritzing 1.0.5)
breadboards: 1

parts:
  MCU1 = Raspberry Pi Zero
  M1 = fc-51 [package=THT]
  M2 = fc-51 [package=THT]
  S1 = Pushbutton [package="[THT]"]

nets:
  N1: MCU1.pin_2, MCU1.pin_4, M1.pin3
  N2: MCU1.pin_3, M1.pin2, M2.pin2, S1.Pin_3, S1.Pin_4
  N3: MCU1.pin_8, S1.Pin_1, S1.Pin_2
  N4: MCU1.pin_14, M1.pin1
  N5: MCU1.pin_26, M2.pin1
  N6: MCU1.pin_40, M2.pin3

notes:
  IR TRANSMITTER ( 5 V )
  IR RECEIVER ( 3.3 V )
